# Fritzing sketch Schematic (saved by Fritzing 0.9.3b)

parts:
  J1 = female pin header, 16 pins [form="♀ (female)"]
  J2 = female pin header, 16 pins [form="♀ (female)"]
  Part1 = Adafruit BME680
  Part2 = FC-28 Soil Hygrometer Module
  Part3 = FC-28 Soil Hygrometer Module - Probe
  Part4 = Adafruit TSL2561 [part_number="Adafruit #439"]

nets:
  N1: J1.pin2, Part4.GND
  N2: J1.pin11, Part4.VIN
  N3: J1.pin12, Part2.AO
  N4: J1.pin13, Part1.3.3V
  N5: J1.pin16, Part2.GND
  N6: J2.pin1, Part1.SCK/SCL, Part1.SDO/ADR, Part4.SCL
  N7: J2.pin2, Part1.SDI/SDA, Part1.CS, Part4.SDA
  N8: J2.pin4, Part1.GND
  N9: J2.pin15, Part2.VCC
  N10: Part2.POS, Part3.POS
  N11: Part2.NEG, Part3.NEG

custom parts:
  FC-28 Soil Hygrometer Module: The FC-28 is a soil hygrometer module that uses the Texas Instruments LM393 comparator chip to provide an analog measurement of soil humidity. The digital output is high when soil moisture is over a certain threshold, as determined by adjusting the potentiometer.
  FC-28 Soil Hygrometer Module - Probe: The FC-28 is a soil hygrometer module that uses the Texas Instruments LM393 comparator chip to provide an analog measurement of soil humidity.
  Adafruit TSL2561: The TSL2561 luminosity sensor is an advanced digital light sensor, ideal for use in a wide range of light situations. Compared to low cost CdS cells, this sensor is more precise, allowing for exact lux calculations and can be configured for different gain/timing ranges to detect light ranges from up to 0.1 - 40,000+ Lux on the fly. The best part of this sensor is that it contains both infrared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
